// Logisim project circ_maurício.circ as structural Verilog: 1 circuit, main circuit main
module main (
  input  A,
  input  B,
  input  C,
  input  D,
  output S1,
  output S2,
  output S3,
  output S4
);

  wire and_1_out, and_2_out, and_3_out, and_4_out, and_5_out, and_6_out, and_7_out, and_8_out, not_1_out,
       not_2_out, not_3_out, not_4_out, or_1_out, or_2_out, or_3_out, or_4_out, or_5_out, or_6_out, or_7_out,
       or_8_out;

  not not_1 (not_1_out, A);
  not not_2 (not_2_out, B);
  not not_3 (not_3_out, C);
  not not_4 (not_4_out, D);
  or or_1 (or_1_out, B, not_4_out);
  or or_2 (or_2_out, D, not_2_out);
  or or_3 (or_3_out, not_4_out, B);
  or or_4 (or_4_out, not_3_out, D);
  and and_1 (and_1_out, not_4_out, B);
  and and_2 (and_2_out, not_3_out, or_1_out);
  and and_3 (and_3_out, not_2_out, D);
  and and_4 (and_4_out, C, or_2_out);
  and and_5 (and_5_out, not_4_out, B);
  and and_6 (and_6_out, C, or_3_out);
  and and_7 (and_7_out, D, not_3_out);
  and and_8 (and_8_out, not_2_out, or_4_out);
  or or_5 (or_5_out, and_1_out, and_2_out);
  or or_6 (or_6_out, and_3_out, and_4_out);
  or or_7 (or_7_out, and_5_out, and_6_out);
  or or_8 (or_8_out, and_7_out, and_8_out);
  and and_9 (S1, not_1_out, or_5_out);
  and and_10 (S2, not_1_out, or_6_out);
  and and_11 (S3, not_1_out, or_7_out);
  and and_12 (S4, not_1_out, or_8_out);
endmodule
