// Logisim project tarefa_tr2_02.circ as structural Verilog: 1 circuit, main circuit main
module main (
  input  in_1,
  input  in_2,
  output out_3,
  output out_4
);

  wire and_1_out, nand_1_out, nor_1_out, not_1_out, not_2_out, not_4_out;

  not not_1 (not_1_out, in_1);
  not not_2 (not_2_out, not_1_out);
  not not_3 (out_4, in_2);
  not not_4 (not_4_out, in_1);
  nor nor_1 (nor_1_out, in_1, not_4_out);
  nand nand_1 (nand_1_out, not_2_out, not_4_out);
  and and_1 (and_1_out, nor_1_out, nand_1_out);
  nor nor_2 (out_3, not_2_out, and_1_out);
endmodule
